// Logisim project Palindrom.circ as structural Verilog: 3 circuits, main circuit main
module main (
  input  in_1,
  input  in_2,
  input  in_3,
  input  in_4,
  input  in_5,
  input  in_6,
  input  in_7,
  input  in_8,
  output out_9
);

  Palindrome palindrome_1 (
    .in_1(in_8), .in_2(in_7), .in_3(in_6), .in_4(in_5), .in_5(in_4), .in_6(in_3), .in_7(in_2), .in_8(in_1),
    .out_9(out_9));
endmodule

module Palindrome (
  input  in_1,
  input  in_2,
  input  in_3,
  input  in_4,
  input  in_5,
  input  in_6,
  input  in_7,
  input  in_8,
  output out_9
);

  wire xnor_1_out, xnor_2_out, xnor_3_out, xnor_4_out;

  xnor xnor_1 (xnor_1_out, in_4, in_5);
  xnor xnor_2 (xnor_2_out, in_3, in_6);
  xnor xnor_3 (xnor_3_out, in_2, in_7);
  xnor xnor_4 (xnor_4_out, in_1, in_8);
  and and_1 (out_9, xnor_1_out, xnor_2_out, xnor_3_out, xnor_4_out);
endmodule

module Rock_Paper_Scissors (
  input  Rock,
  input  Paper,
  input  Scissors,
  input  in_4,
  input  in_5,
  input  in_6,
  output out_7,
  output out_8
);

  wire and_1_out, and_2_out, and_3_out, and_4_out, and_5_out, and_6_out;

  and and_1 (and_1_out, Scissors, in_4);
  and and_2 (and_2_out, Rock, in_6);
  and and_3 (and_3_out, Paper, in_4);
  and and_4 (and_4_out, Scissors, in_4);
  and and_5 (and_5_out, Rock, in_5);
  and and_6 (and_6_out, Paper, in_6);
  or or_1 (out_7, and_1_out, and_2_out, and_3_out);
  or or_2 (out_8, and_4_out, and_5_out, and_6_out);
endmodule
